# Fritzing sketch Hand Wiring (saved by Fritzing 0.9.6b)

parts:
  Part2 = 16-Channel 12-bit PWM Servo Driver - I2C [part_number=815]
  Part3 = MyoWare Cable Shield
  J2 = Basic Servo
  J4 = Basic Servo
  J5 = Basic Servo
  J6 = Basic Servo
  BATT1 = LiPoly Battery (1300mAh)
  Part4 = Arduino Uno (Rev3)
  J3 = Basic Servo

nets:
  N1: Part2.PWRIN, BATT1.positive
  GND: Part2.GND, Part3.GND, J2.gnd, J4.gnd, J5.gnd, J6.gnd, BATT1.negative, Part4.GND, J3.gnd
  N2: Part2.PWM4, J3.pulse
  VCC: Part2.5.0V, J2.vcc, J4.vcc, J5.vcc, J6.vcc, Part4.5V, J3.vcc
  N3: Part2.PWM3, J5.pulse
  N4: Part2.PWM2, J4.pulse
  N5: Part2.PWM1, J6.pulse
  N6: Part2.PWM0, J2.pulse
  N7: Part2.SDA, Part4.A5/SCL
  N8: Part2.SCL, Part4.A4/SDA
  VCC_2: Part3.VCC, Part4.3V3
  N9: Part3.SIG, Part4.A0

custom parts:
  16-Channel 12-bit PWM Servo Driver - I2C: You want to make a cool robot, maybe a hexapod walker, or maybe just a piece of art with a lot of moving parts. Or maybe you want to drive a lot of LEDs with precise PWM output. Using only two pins, control 16 free-running PWM outputs! You can even chain up 62 breakouts to control up to 992 PWM outputs.
  LiPoly Battery (1300mAh): Lithium Ion Polymer Battery (1300mAh)
